# Fritzing sketch auto_splash_catapult (saved by Fritzing 0.9.3b)
breadboards: 1

parts:
  元件1 = Arduino Uno (Rev3) - ICSP
  J2 = Basic Servo  # not connected
  J1 = Basic Servo

nets:
  N1: 元件1.D9_PWM, J1.pulse
